// Digital circuit Negcao.dig as structural Verilog
module Negcao (
  input  a0,
  input  a1,
  input  a2,
  input  a3,
  input  a4,
  input  a5,
  input  a6,
  input  a7,
  input  a8,
  input  a9,
  input  a10,
  input  a11,
  input  a12,
  input  a13,
  input  a14,
  input  a15,
  output s0,
  output s1,
  output s2,
  output s3,
  output s4,
  output s5,
  output s6,
  output s7,
  output s8,
  output s9,
  output s10,
  output s11,
  output s12,
  output s13,
  output s14,
  output s15
);

  not not_1 (s0, a0);
  not not_2 (s1, a1);
  not not_3 (s2, a2);
  not not_4 (s3, a3);
  not not_5 (s4, a4);
  not not_6 (s5, a5);
  not not_7 (s6, a6);
  not not_8 (s7, a7);
  not not_9 (s8, a8);
  not not_10 (s9, a9);
  not not_11 (s10, a10);
  not not_12 (s11, a11);
  not not_13 (s12, a12);
  not not_14 (s13, a13);
  not not_15 (s14, a14);
  not not_16 (s15, a15);
endmodule
