// Digital circuit Or.dig as structural Verilog
module Or (
  input  a0,
  input  a1,
  input  a2,
  input  a3,
  input  a4,
  input  a5,
  input  a6,
  input  a7,
  input  a8,
  input  a9,
  input  a10,
  input  a11,
  input  a12,
  input  a13,
  input  a14,
  input  a15,
  input  b0,
  input  b1,
  input  b2,
  input  b3,
  input  b4,
  input  b5,
  input  b6,
  input  b7,
  input  b8,
  input  b9,
  input  b10,
  input  b11,
  input  b12,
  input  b13,
  input  b14,
  input  b15,
  output s0,
  output s1,
  output s2,
  output s3,
  output s4,
  output s5,
  output s6,
  output s7,
  output s8,
  output s9,
  output s10,
  output s11,
  output s12,
  output s13,
  output s14,
  output s15
);

  or or_1 (s0, a0, b0);
  or or_2 (s1, a1, b1);
  or or_3 (s2, a2, b2);
  or or_4 (s3, a3, b3);
  or or_5 (s4, a4, b4);
  or or_6 (s5, a5, b5);
  or or_7 (s6, a6, b6);
  or or_8 (s7, a7, b7);
  or or_9 (s8, a8, b8);
  or or_10 (s9, a9, b9);
  or or_11 (s10, a10, b10);
  or or_12 (s11, a11, b11);
  or or_13 (s12, a12, b12);
  or or_14 (s14, a14, b14);
  or or_15 (s15, a15, b15);
  or or_16 (s13, a13, b13);
endmodule
