// Digital circuit ULA.dig as structural Verilog
module ULA (
  input  _0,
  input  _1,
  input  [15:0] A,
  input  [15:0] B,
  input  [2:0] F,
  output OVFL,
  output Zero,
  output Negativo,
  output [15:0] S
);

  wire and_1_out, and_2_out, and_3_s0, and_3_s1, and_3_s2, and_3_s3, and_3_s4, and_3_s5, and_3_s6, and_3_s7,
       and_3_s8, and_3_s9, and_3_s10, and_3_s11, and_3_s12, and_3_s13, and_3_s14, and_3_s15, deslocador_1_s0,
       deslocador_1_s1, deslocador_1_s2, deslocador_1_s3, deslocador_1_s4, deslocador_1_s5, deslocador_1_s6,
       deslocador_1_s7, deslocador_1_s8, deslocador_1_s9, deslocador_1_s10, deslocador_1_s11,
       deslocador_1_s12, deslocador_1_s13, deslocador_1_s14, deslocador_1_s15, deslocador_2_s0,
       deslocador_2_s1, deslocador_2_s2, deslocador_2_s3, deslocador_2_s4, deslocador_2_s5, deslocador_2_s6,
       deslocador_2_s7, deslocador_2_s8, deslocador_2_s9, deslocador_2_s10, deslocador_2_s11,
       deslocador_2_s12, deslocador_2_s13, deslocador_2_s14, deslocador_2_s15, negcao_1_s0, negcao_1_s1,
       negcao_1_s2, negcao_1_s3, negcao_1_s4, negcao_1_s5, negcao_1_s6, negcao_1_s7, negcao_1_s8,
       negcao_1_s9, negcao_1_s10, negcao_1_s11, negcao_1_s12, negcao_1_s13, negcao_1_s14, negcao_1_s15,
       or_2_s0, or_2_s1, or_2_s2, or_2_s3, or_2_s4, or_2_s5, or_2_s6, or_2_s7, or_2_s8, or_2_s9, or_2_s10,
       or_2_s11, or_2_s12, or_2_s13, or_2_s14, or_2_s15, subtrator_1_ovfl, subtrator_1_s0, subtrator_1_s1,
       subtrator_1_s2, subtrator_1_s3, subtrator_1_s4, subtrator_1_s5, subtrator_1_s6, subtrator_1_s7,
       subtrator_1_s8, subtrator_1_s9, subtrator_1_s10, subtrator_1_s11, subtrator_1_s12, subtrator_1_s13,
       subtrator_1_s14, subtrator_1_s15, xor_1_s0, xor_1_s1, xor_1_s2, xor_1_s3, xor_1_s4, xor_1_s5,
       xor_1_s6, xor_1_s7, xor_1_s8, xor_1_s9, xor_1_s10, xor_1_s11, xor_1_s12, xor_1_s13, xor_1_s14,
       xor_1_s15;

  and and_1 (and_1_out, ~F[2], ~F[1], F[0]);  // And
  and and_2 (and_2_out, _0, ~F[0], ~F[1], ~F[2]);  // And
  or or_1 (OVFL, and_2_out, subtrator_1_ovfl);
  subtrator subtrator_1 (
    .a0(A[0]), .b0(B[0]), .a1(A[1]), .b1(B[1]), .a2(A[2]), .b2(B[2]), .a3(A[3]), .b3(B[3]), .a4(A[4]),
    .b4(B[4]), .a5(A[5]), .b5(B[5]), .a6(A[6]), .b6(B[6]), .a7(A[7]), .b7(B[7]), .a8(A[8]), .b8(B[8]),
    .a9(A[9]), .b9(B[9]), .a10(A[10]), .b10(B[10]), .a11(A[11]), .b11(B[11]), .a12(A[12]), .b12(B[12]),
    .a13(A[13]), .b13(B[13]), .a14(A[14]), .b14(B[14]), .a15(A[15]), .b15(B[15]), ._0(_0), ._1(_1),
    .vem(and_1_out), .s8(subtrator_1_s8), .s9(subtrator_1_s9), .s10(subtrator_1_s10), .s11(subtrator_1_s11),
    .s12(subtrator_1_s12), .s13(subtrator_1_s13), .s14(subtrator_1_s14), .s15(subtrator_1_s15),
    .s0(subtrator_1_s0), .s1(subtrator_1_s1), .s2(subtrator_1_s2), .s3(subtrator_1_s3), .s4(subtrator_1_s4),
    .s5(subtrator_1_s5), .s6(subtrator_1_s6), .s7(subtrator_1_s7), .OVFL(subtrator_1_ovfl));
  deslocador deslocador_1 (
    .lt__lt(_1), .a0(A[0]), .a1(A[1]), .a2(A[2]), .a3(A[3]), .a4(A[4]), .a5(A[5]), .a6(A[6]), .a7(A[7]),
    .a8(A[8]), .a9(A[9]), .a10(A[10]), .a11(A[11]), .a12(A[12]), .a13(A[13]), .a14(A[14]), .a15(A[15]),
    .gt__gt(_0), .s0(deslocador_1_s0), .s1(deslocador_1_s1), .s2(deslocador_1_s2), .s4(deslocador_1_s4),
    .s5(deslocador_1_s5), .s6(deslocador_1_s6), .s7(deslocador_1_s7), .s8(deslocador_1_s8),
    .s9(deslocador_1_s9), .s10(deslocador_1_s10), .s11(deslocador_1_s11), .s12(deslocador_1_s12),
    .s13(deslocador_1_s13), .s14(deslocador_1_s14), .s15(deslocador_1_s15), .s3(deslocador_1_s3));
  deslocador deslocador_2 (
    .lt__lt(_0), .a0(A[0]), .a1(A[1]), .a2(A[2]), .a3(A[3]), .a4(A[4]), .a5(A[5]), .a6(A[6]), .a7(A[7]),
    .a8(A[8]), .a9(A[9]), .a10(A[10]), .a11(A[11]), .a12(A[12]), .a13(A[13]), .a14(A[14]), .a15(A[15]),
    .gt__gt(_1), .s0(deslocador_2_s0), .s1(deslocador_2_s1), .s2(deslocador_2_s2), .s4(deslocador_2_s4),
    .s5(deslocador_2_s5), .s6(deslocador_2_s6), .s7(deslocador_2_s7), .s8(deslocador_2_s8),
    .s9(deslocador_2_s9), .s10(deslocador_2_s10), .s11(deslocador_2_s11), .s12(deslocador_2_s12),
    .s13(deslocador_2_s13), .s14(deslocador_2_s14), .s15(deslocador_2_s15), .s3(deslocador_2_s3));
  Negcao negcao_1 (
    .a0(A[0]), .a1(A[1]), .a2(A[2]), .a3(A[3]), .a4(A[4]), .a5(A[5]), .a6(A[6]), .a7(A[7]), .a8(A[8]),
    .a9(A[9]), .a10(A[10]), .a11(A[11]), .a12(A[12]), .a13(A[13]), .a14(A[14]), .a15(A[15]),
    .s0(negcao_1_s0), .s1(negcao_1_s1), .s2(negcao_1_s2), .s3(negcao_1_s3), .s4(negcao_1_s4),
    .s5(negcao_1_s5), .s6(negcao_1_s6), .s7(negcao_1_s7), .s8(negcao_1_s8), .s9(negcao_1_s9),
    .s10(negcao_1_s10), .s11(negcao_1_s11), .s12(negcao_1_s12), .s13(negcao_1_s13), .s14(negcao_1_s14),
    .s15(negcao_1_s15));
  \and  and_3 (
    .a0(A[0]), .a1(A[1]), .a2(A[2]), .a3(A[3]), .a4(A[4]), .a5(A[5]), .a6(A[6]), .a7(A[7]), .a8(A[8]),
    .a9(A[9]), .a10(A[10]), .a11(A[11]), .a12(A[12]), .a13(A[13]), .a14(A[14]), .a15(A[15]), .b0(B[0]),
    .b1(B[1]), .b2(B[2]), .b3(B[3]), .b4(B[4]), .b5(B[5]), .b6(B[6]), .b7(B[7]), .b8(B[8]), .b9(B[9]),
    .b10(B[10]), .b11(B[11]), .b12(B[12]), .b13(B[13]), .b14(B[14]), .b15(B[15]), .s0(and_3_s0),
    .s1(and_3_s1), .s2(and_3_s2), .s3(and_3_s3), .s4(and_3_s4), .s5(and_3_s5), .s6(and_3_s6), .s7(and_3_s7),
    .s8(and_3_s8), .s9(and_3_s9), .s10(and_3_s10), .s11(and_3_s11), .s12(and_3_s12), .s13(and_3_s13),
    .s14(and_3_s14), .s15(and_3_s15));
  Xor xor_1 (
    .a0(A[0]), .a1(A[1]), .a2(A[2]), .a3(A[3]), .a4(A[4]), .a5(A[5]), .a6(A[6]), .a7(A[7]), .a8(A[8]),
    .a9(A[9]), .a10(A[10]), .a11(A[11]), .a12(A[12]), .a13(A[13]), .a14(A[14]), .a15(A[15]), .b0(B[0]),
    .b1(B[1]), .b2(B[2]), .b3(B[3]), .b4(B[4]), .b5(B[5]), .b6(B[6]), .b7(B[7]), .b8(B[8]), .b9(B[9]),
    .b10(B[10]), .b11(B[11]), .b12(B[12]), .b13(B[13]), .b14(B[14]), .b15(B[15]), .s0(xor_1_s0),
    .s1(xor_1_s1), .s2(xor_1_s2), .s3(xor_1_s3), .s4(xor_1_s4), .s5(xor_1_s5), .s6(xor_1_s6), .s7(xor_1_s7),
    .s8(xor_1_s8), .s9(xor_1_s9), .s10(xor_1_s10), .s11(xor_1_s11), .s12(xor_1_s12), .s13(xor_1_s13),
    .s14(xor_1_s14), .s15(xor_1_s15));
  Or or_2 (
    .a0(A[0]), .a1(A[1]), .a2(A[2]), .a3(A[3]), .a4(A[4]), .a5(A[5]), .a6(A[6]), .a7(A[7]), .a8(A[8]),
    .a9(A[9]), .a10(A[10]), .a11(A[11]), .a12(A[12]), .a13(A[13]), .a14(A[14]), .a15(A[15]), .b0(B[0]),
    .b1(B[1]), .b2(B[2]), .b3(B[3]), .b4(B[4]), .b5(B[5]), .b6(B[6]), .b7(B[7]), .b8(B[8]), .b9(B[9]),
    .b10(B[10]), .b11(B[11]), .b12(B[12]), .b13(B[13]), .b14(B[14]), .b15(B[15]), .s0(or_2_s0), .s1(or_2_s1),
    .s2(or_2_s2), .s3(or_2_s3), .s4(or_2_s4), .s5(or_2_s5), .s6(or_2_s6), .s7(or_2_s7), .s8(or_2_s8),
    .s9(or_2_s9), .s10(or_2_s10), .s11(or_2_s11), .s12(or_2_s12), .s13(or_2_s13), .s14(or_2_s14),
    .s15(or_2_s15));
  mux8 mux8_1 (
    .a0(or_2_s15), .a1(xor_1_s15), .a2(and_3_s15), .a3(negcao_1_s15), .a4(deslocador_2_s15),
    .a5(deslocador_1_s15), .a6(subtrator_1_s15), .a7(subtrator_1_s15), .s0(F[0]), .s1(F[1]), .s2(F[2]),
    .s(Negativo));
  mux8 mux8_2 (
    .a0(or_2_s14), .a1(xor_1_s14), .a2(and_3_s14), .a3(negcao_1_s14), .a4(deslocador_2_s14),
    .a5(deslocador_1_s14), .a6(subtrator_1_s14), .a7(subtrator_1_s14), .s0(F[0]), .s1(F[1]), .s2(F[2]),
    .s(S[14]));
  mux8 mux8_3 (
    .a0(or_2_s13), .a1(xor_1_s13), .a2(and_3_s13), .a3(negcao_1_s13), .a4(deslocador_2_s13),
    .a5(deslocador_1_s13), .a6(subtrator_1_s13), .a7(subtrator_1_s13), .s0(F[0]), .s1(F[1]), .s2(F[2]),
    .s(S[13]));
  mux8 mux8_4 (
    .a0(or_2_s12), .a1(xor_1_s12), .a2(and_3_s12), .a3(negcao_1_s12), .a4(deslocador_2_s12),
    .a5(deslocador_1_s12), .a6(subtrator_1_s12), .a7(subtrator_1_s12), .s0(F[0]), .s1(F[1]), .s2(F[2]),
    .s(S[12]));
  mux8 mux8_5 (
    .a0(or_2_s11), .a1(xor_1_s11), .a2(and_3_s11), .a3(negcao_1_s11), .a4(deslocador_2_s11),
    .a5(deslocador_1_s11), .a6(subtrator_1_s11), .a7(subtrator_1_s11), .s0(F[0]), .s1(F[1]), .s2(F[2]),
    .s(S[11]));
  nor nor_1 (Zero, S[0], S[1], S[2], S[3], S[4], S[5], S[6], S[7], S[8], S[9], S[10], S[11], S[12], S[13], S[14], Negativo);
  mux8 mux8_6 (
    .a0(or_2_s10), .a1(xor_1_s10), .a2(and_3_s10), .a3(negcao_1_s10), .a4(deslocador_2_s10),
    .a5(deslocador_1_s10), .a6(subtrator_1_s10), .a7(subtrator_1_s10), .s0(F[0]), .s1(F[1]), .s2(F[2]),
    .s(S[10]));
  mux8 mux8_7 (
    .a0(or_2_s9), .a1(xor_1_s9), .a2(and_3_s9), .a3(negcao_1_s9), .a4(deslocador_2_s9), .a5(deslocador_1_s9),
    .a6(subtrator_1_s9), .a7(subtrator_1_s9), .s0(F[0]), .s1(F[1]), .s2(F[2]), .s(S[9]));
  mux8 mux8_8 (
    .a0(or_2_s8), .a1(xor_1_s8), .a2(and_3_s8), .a3(negcao_1_s8), .a4(deslocador_2_s8), .a5(deslocador_1_s8),
    .a6(subtrator_1_s8), .a7(subtrator_1_s8), .s0(F[0]), .s1(F[1]), .s2(F[2]), .s(S[8]));
  mux8 mux8_9 (
    .a0(or_2_s7), .a1(xor_1_s7), .a2(and_3_s7), .a3(negcao_1_s7), .a4(deslocador_2_s7), .a5(deslocador_1_s7),
    .a6(subtrator_1_s7), .a7(subtrator_1_s7), .s0(F[0]), .s1(F[1]), .s2(F[2]), .s(S[7]));
  mux8 mux8_10 (
    .a0(or_2_s6), .a1(xor_1_s6), .a2(and_3_s6), .a3(negcao_1_s6), .a4(deslocador_2_s6), .a5(deslocador_1_s6),
    .a6(subtrator_1_s6), .a7(subtrator_1_s6), .s0(F[0]), .s1(F[1]), .s2(F[2]), .s(S[6]));
  mux8 mux8_11 (
    .a0(or_2_s5), .a1(xor_1_s5), .a2(and_3_s5), .a3(negcao_1_s5), .a4(deslocador_2_s5), .a5(deslocador_1_s5),
    .a6(subtrator_1_s5), .a7(subtrator_1_s5), .s0(F[0]), .s1(F[1]), .s2(F[2]), .s(S[5]));
  mux8 mux8_12 (
    .a0(or_2_s4), .a1(xor_1_s4), .a2(and_3_s4), .a3(negcao_1_s4), .a4(deslocador_2_s4), .a5(deslocador_1_s4),
    .a6(subtrator_1_s4), .a7(subtrator_1_s4), .s0(F[0]), .s1(F[1]), .s2(F[2]), .s(S[4]));
  mux8 mux8_13 (
    .a0(or_2_s3), .a1(xor_1_s3), .a2(and_3_s3), .a3(negcao_1_s3), .a4(deslocador_2_s3), .a5(deslocador_1_s3),
    .a6(subtrator_1_s3), .a7(subtrator_1_s3), .s0(F[0]), .s1(F[1]), .s2(F[2]), .s(S[3]));
  mux8 mux8_14 (
    .a0(or_2_s2), .a1(xor_1_s2), .a2(and_3_s2), .a3(negcao_1_s2), .a4(deslocador_2_s2), .a5(deslocador_1_s2),
    .a6(subtrator_1_s2), .a7(subtrator_1_s2), .s0(F[0]), .s1(F[1]), .s2(F[2]), .s(S[2]));
  mux8 mux8_15 (
    .a0(or_2_s1), .a1(xor_1_s1), .a2(and_3_s1), .a3(negcao_1_s1), .a4(deslocador_2_s1), .a5(deslocador_1_s1),
    .a6(subtrator_1_s1), .a7(subtrator_1_s1), .s0(F[0]), .s1(F[1]), .s2(F[2]), .s(S[1]));
  mux8 mux8_16 (
    .a0(or_2_s0), .a1(xor_1_s0), .a2(and_3_s0), .a3(negcao_1_s0), .a4(deslocador_2_s0), .a5(deslocador_1_s0),
    .a6(subtrator_1_s0), .a7(subtrator_1_s0), .s0(F[0]), .s1(F[1]), .s2(F[2]), .s(S[0]));

  assign S[15] = Negativo;

  // Notes on the sheet:
  //   _1: default 1
endmodule
