// Digital circuit and.dig as structural Verilog
module \and  (
  input  a0,
  input  a1,
  input  a2,
  input  a3,
  input  a4,
  input  a5,
  input  a6,
  input  a7,
  input  a8,
  input  a9,
  input  a10,
  input  a11,
  input  a12,
  input  a13,
  input  a14,
  input  a15,
  input  b0,
  input  b1,
  input  b2,
  input  b3,
  input  b4,
  input  b5,
  input  b6,
  input  b7,
  input  b8,
  input  b9,
  input  b10,
  input  b11,
  input  b12,
  input  b13,
  input  b14,
  input  b15,
  output s0,
  output s1,
  output s2,
  output s3,
  output s4,
  output s5,
  output s6,
  output s7,
  output s8,
  output s9,
  output s10,
  output s11,
  output s12,
  output s13,
  output s14,
  output s15
);

  and and_1 (s0, a0, b0);
  and and_2 (s1, a1, b1);
  and and_3 (s2, a2, b2);
  and and_4 (s3, a3, b3);
  and and_5 (s4, a4, b4);
  and and_6 (s5, a5, b5);
  and and_7 (s6, a6, b6);
  and and_8 (s7, a7, b7);
  and and_9 (s8, a8, b8);
  and and_10 (s9, a9, b9);
  and and_11 (s10, a10, b10);
  and and_12 (s11, a11, b11);
  and and_13 (s12, a12, b12);
  and and_14 (s14, a14, b14);
  and and_15 (s15, a15, b15);
  and and_16 (s13, a13, b13);
endmodule
