// Digital circuit deslocador.dig as structural Verilog
module deslocador (
  input  lt__lt,
  input  a0,
  input  a1,
  input  a2,
  input  a3,
  input  a4,
  input  a5,
  input  a6,
  input  a7,
  input  a8,
  input  a9,
  input  a10,
  input  a11,
  input  a12,
  input  a13,
  input  a14,
  input  a15,
  input  gt__gt,
  output s0,
  output s1,
  output s2,
  output s4,
  output s5,
  output s6,
  output s7,
  output s8,
  output s9,
  output s10,
  output s11,
  output s12,
  output s13,
  output s14,
  output s15,
  output s3
);

  wire and_1_out, and_3_out, and_4_out, and_5_out, and_6_out, and_7_out, and_8_out, and_9_out, and_10_out,
       and_11_out, and_12_out, and_13_out, and_14_out, and_15_out, and_16_out, and_17_out, and_18_out,
       and_19_out, and_20_out, and_21_out, and_22_out, and_23_out, and_24_out, and_25_out, and_26_out,
       and_27_out, and_28_out, and_30_out;

  and and_1 (and_1_out, a15, gt__gt);
  and and_2 (s15, lt__lt, a14);
  and and_3 (and_3_out, a14, gt__gt);
  and and_4 (and_4_out, lt__lt, a13);
  and and_5 (and_5_out, a13, gt__gt);
  and and_6 (and_6_out, lt__lt, a12);
  and and_7 (and_7_out, a12, gt__gt);
  and and_8 (and_8_out, lt__lt, a11);
  and and_9 (and_9_out, a11, gt__gt);
  and and_10 (and_10_out, lt__lt, a10);
  and and_11 (and_11_out, a10, gt__gt);
  and and_12 (and_12_out, lt__lt, a9);
  and and_13 (and_13_out, a9, gt__gt);
  and and_14 (and_14_out, lt__lt, a8);
  and and_15 (and_15_out, a8, gt__gt);
  and and_16 (and_16_out, lt__lt, a7);
  and and_17 (and_17_out, a7, gt__gt);
  and and_18 (and_18_out, lt__lt, a6);
  and and_19 (and_19_out, a6, gt__gt);
  and and_20 (and_20_out, lt__lt, a5);
  and and_21 (and_21_out, a5, gt__gt);
  and and_22 (and_22_out, lt__lt, a4);
  and and_23 (and_23_out, a4, gt__gt);
  and and_24 (and_24_out, lt__lt, a3);
  and and_25 (and_25_out, a3, gt__gt);
  and and_26 (and_26_out, lt__lt, a2);
  and and_27 (and_27_out, a2, gt__gt);
  and and_28 (and_28_out, lt__lt, a1);
  and and_29 (s0, a1, gt__gt);
  and and_30 (and_30_out, lt__lt, a0);
  or or_1 (s10, and_9_out, and_12_out);
  or or_2 (s9, and_11_out, and_14_out);
  or or_3 (s8, and_13_out, and_16_out);
  or or_4 (s7, and_15_out, and_18_out);
  or or_5 (s6, and_17_out, and_20_out);
  or or_6 (s5, and_19_out, and_22_out);
  or or_7 (s4, and_21_out, and_24_out);
  or or_8 (s3, and_23_out, and_26_out);
  or or_9 (s2, and_25_out, and_28_out);
  or or_10 (s1, and_27_out, and_30_out);
  or or_11 (s14, and_1_out, and_4_out);
  or or_12 (s13, and_3_out, and_6_out);
  or or_13 (s12, and_5_out, and_8_out);
  or or_14 (s11, and_7_out, and_10_out);
endmodule
