// Digital circuit mult2.dig as structural Verilog
module mult2 (
  input  a0,
  input  a1,
  input  s0,
  output s
);

  wire and_1_out, and_2_out;

  and and_1 (and_1_out, a0, s0);
  and and_2 (and_2_out, a1, ~s0);  // And
  or or_1 (s, and_1_out, and_2_out);
endmodule
