// Digital circuit mulx4.dig as structural Verilog
module mulx4 (
  input  a0,
  input  a1,
  input  a2,
  input  a3,
  input  s0,
  input  s1,
  output s
);

  wire mult2_1_s, mult2_2_s;

  mult2 mult2_1 (.a0(a0), .a1(a1), .s0(s0), .s(mult2_1_s));
  mult2 mult2_2 (.a0(a2), .a1(a3), .s0(s0), .s(mult2_2_s));
  mult2 mult2_3 (.a0(mult2_1_s), .a1(mult2_2_s), .s0(s1), .s(s));
endmodule
