// Digital circuit mux8.dig as structural Verilog
module mux8 (
  input  a0,
  input  a1,
  input  a2,
  input  a3,
  input  a4,
  input  a5,
  input  a6,
  input  a7,
  input  s0,
  input  s1,
  input  s2,
  output s
);

  wire mulx4_1_s, mulx4_2_s;

  mulx4 mulx4_1 (.a0(a0), .a1(a1), .a2(a2), .a3(a3), .s0(s0), .s1(s1), .s(mulx4_1_s));
  mulx4 mulx4_2 (.a0(a4), .a1(a5), .a2(a6), .a3(a7), .s0(s0), .s1(s1), .s(mulx4_2_s));
  mult2 mult2_1 (.a0(mulx4_1_s), .a1(mulx4_2_s), .s0(s2), .s(s));
endmodule
