// Digital circuit soma8.dig as structural Verilog
module soma8 (
  input  vem,
  input  b0,
  input  a0,
  input  b1,
  input  a1,
  input  b2,
  input  a2,
  input  b3,
  input  a3,
  input  b4,
  input  a4,
  input  b5,
  input  a5,
  input  b6,
  input  a6,
  input  b7,
  input  a7,
  output s0,
  output s1,
  output s2,
  output s3,
  output s4,
  output s5,
  output s6,
  output s7,
  output vai
);

  wire somador_2_vai, somador_3_vai, somador_4_vai, somador_5_vai, somador_6_vai, somador_7_vai,
       somador_8_vai;

  somador somador_1 (.a(a7), .b(b7), .vem(somador_2_vai), .s(s7), .vai(vai));
  somador somador_2 (.a(a6), .b(b6), .vem(somador_3_vai), .s(s6), .vai(somador_2_vai));
  somador somador_3 (.a(a5), .b(b5), .vem(somador_4_vai), .s(s5), .vai(somador_3_vai));
  somador somador_4 (.a(a4), .b(b4), .vem(somador_5_vai), .s(s4), .vai(somador_4_vai));
  somador somador_5 (.a(a3), .b(b3), .vem(somador_6_vai), .s(s3), .vai(somador_5_vai));
  somador somador_6 (.a(a2), .b(b2), .vem(somador_7_vai), .s(s2), .vai(somador_6_vai));
  somador somador_7 (.a(a1), .b(b1), .vem(somador_8_vai), .s(s1), .vai(somador_7_vai));
  somador somador_8 (.a(a0), .b(b0), .vem(vem), .s(s0), .vai(somador_8_vai));
endmodule

/* Test case:
vem a b vai s
0   0 0  0  0
*/
