// Digital circuit soma8inv.dig as structural Verilog
module soma8inv (
  input  vem,
  input  b0,
  input  a0,
  input  b1,
  input  a1,
  input  b2,
  input  a2,
  input  b3,
  input  a3,
  input  b4,
  input  a4,
  input  b5,
  input  a5,
  input  b6,
  input  a6,
  input  b7,
  input  a7,
  input  inv,
  output s0,
  output s1,
  output s2,
  output s3,
  output s4,
  output s5,
  output s6,
  output s7,
  output vai,
  output Ovfl
);

  wire somador_2_vai, somador_3_vai, somador_4_vai, somador_5_vai, somador_6_vai, somador_7_vai,
       somador_8_vai, xor_2_out, xor_3_out, xor_4_out, xor_5_out, xor_6_out, xor_7_out, xor_8_out, xor_9_out;

  xor xor_1 (Ovfl, somador_2_vai, vai);
  xor xor_2 (xor_2_out, inv, b7);
  somador somador_1 (.a(a7), .b(xor_2_out), .vem(somador_2_vai), .s(s7), .vai(vai));
  somador somador_2 (.a(a6), .b(xor_3_out), .vem(somador_3_vai), .s(s6), .vai(somador_2_vai));
  xor xor_3 (xor_3_out, inv, b6);
  somador somador_3 (.a(a5), .b(xor_4_out), .vem(somador_4_vai), .s(s5), .vai(somador_3_vai));
  xor xor_4 (xor_4_out, inv, b5);
  somador somador_4 (.a(a4), .b(xor_5_out), .vem(somador_5_vai), .s(s4), .vai(somador_4_vai));
  xor xor_5 (xor_5_out, inv, b4);
  somador somador_5 (.a(a3), .b(xor_6_out), .vem(somador_6_vai), .s(s3), .vai(somador_5_vai));
  xor xor_6 (xor_6_out, inv, b3);
  xor xor_7 (xor_7_out, inv, b2);
  somador somador_6 (.a(a2), .b(xor_7_out), .vem(somador_7_vai), .s(s2), .vai(somador_6_vai));
  somador somador_7 (.a(a1), .b(xor_8_out), .vem(somador_8_vai), .s(s1), .vai(somador_7_vai));
  xor xor_8 (xor_8_out, inv, b1);
  somador somador_8 (.a(a0), .b(xor_9_out), .vem(vem), .s(s0), .vai(somador_8_vai));
  xor xor_9 (xor_9_out, inv, b0);
endmodule

/* Test case:
vem a b vai s
0   0 0  0  0
*/
