// Digital circuit somador.dig as structural Verilog
module somador (
  input  a,
  input  b,
  input  vem,
  output s,
  output vai
);

  wire and_1_out, and_2_out, and_3_out, xor_1_out;

  xor xor_1 (xor_1_out, a, b);
  and and_1 (and_1_out, a, b);
  and and_2 (and_2_out, b, vem);
  and and_3 (and_3_out, a, vem);
  xor xor_2 (s, xor_1_out, vem);
  or or_1 (vai, and_1_out, and_2_out, and_3_out);
endmodule

/* Test case:
vem a b vai s
0   0 0  0  0
0   0 1  0  1
0   1 0  0  1
0   1 1  1  0
1   0 0  0  1
1   0 1  1  0
1   1 0  1  0
1   1 1  1  1
*/
