// Digital circuit subtrator.dig as structural Verilog
module subtrator (
  input  a0,
  input  b0,
  input  a1,
  input  b1,
  input  a2,
  input  b2,
  input  a3,
  input  b3,
  input  a4,
  input  b4,
  input  a5,
  input  b5,
  input  a6,
  input  b6,
  input  a7,
  input  b7,
  input  a8,
  input  b8,
  input  a9,
  input  b9,
  input  a10,
  input  b10,
  input  a11,
  input  b11,
  input  a12,
  input  b12,
  input  a13,
  input  b13,
  input  a14,
  input  b14,
  input  a15,
  input  b15,
  input  _0,
  input  _1,
  input  vem,
  output s8,
  output s9,
  output s10,
  output s11,
  output s12,
  output s13,
  output s14,
  output s15,
  output s0,
  output s1,
  output s2,
  output s3,
  output s4,
  output s5,
  output s6,
  output s7,
  output OVFL
);

  wire soma8inv_1_vai, soma8inv_2_ovfl, soma8inv_2_s0, soma8inv_2_s1, soma8inv_2_s2, soma8inv_2_s3,
       soma8inv_2_s4, soma8inv_2_s5, soma8inv_2_s6, soma8inv_2_s7, soma8inv_3_ovfl, soma8inv_3_s0,
       soma8inv_3_s1, soma8inv_3_s2, soma8inv_3_s3, soma8inv_3_s4, soma8inv_3_s5, soma8inv_3_s6,
       soma8inv_3_s7;

  mult2 mult2_1 (.a0(soma8inv_2_ovfl), .a1(soma8inv_3_ovfl), .s0(soma8inv_1_vai), .s(OVFL));
  mult2 mult2_2 (.a0(soma8inv_3_s7), .a1(soma8inv_2_s7), .s0(soma8inv_1_vai), .s(s15));
  mult2 mult2_3 (.a0(soma8inv_3_s6), .a1(soma8inv_2_s6), .s0(soma8inv_1_vai), .s(s14));
  mult2 mult2_4 (.a0(soma8inv_3_s5), .a1(soma8inv_2_s5), .s0(soma8inv_1_vai), .s(s13));
  mult2 mult2_5 (.a0(soma8inv_3_s4), .a1(soma8inv_2_s4), .s0(soma8inv_1_vai), .s(s12));
  mult2 mult2_6 (.a0(soma8inv_3_s3), .a1(soma8inv_2_s3), .s0(soma8inv_1_vai), .s(s11));
  soma8inv soma8inv_1 (
    .vem(vem), .b0(b0), .a0(a0), .b1(b1), .a1(a1), .b2(b2), .a2(a2), .b3(b3), .a3(a3), .b4(b4), .a4(a4),
    .b5(b5), .a5(a5), .b6(b6), .a6(a6), .b7(b7), .a7(a7), .inv(vem), .s0(s0), .s1(s1), .s2(s2), .s3(s3),
    .s4(s4), .s5(s5), .s6(s6), .s7(s7), .vai(soma8inv_1_vai));  // open: Ovfl
  mult2 mult2_7 (.a0(soma8inv_3_s2), .a1(soma8inv_2_s2), .s0(soma8inv_1_vai), .s(s10));
  mult2 mult2_8 (.a0(soma8inv_3_s1), .a1(soma8inv_2_s1), .s0(soma8inv_1_vai), .s(s9));
  mult2 mult2_9 (.a0(soma8inv_3_s0), .a1(soma8inv_2_s0), .s0(soma8inv_1_vai), .s(s8));
  soma8inv soma8inv_2 (
    .vem(_0), .b0(b8), .a0(a8), .b1(b9), .a1(a9), .b2(b10), .a2(a10), .b3(b11), .a3(a11), .b4(b12), .a4(a12),
    .b5(b13), .a5(a13), .b6(b14), .a6(a14), .b7(b15), .a7(a15), .inv(vem), .s0(soma8inv_2_s0),
    .s1(soma8inv_2_s1), .s2(soma8inv_2_s2), .s3(soma8inv_2_s3), .s4(soma8inv_2_s4), .s5(soma8inv_2_s5),
    .s6(soma8inv_2_s6), .s7(soma8inv_2_s7), .Ovfl(soma8inv_2_ovfl));  // open: vai
  soma8inv soma8inv_3 (
    .vem(_1), .b0(b8), .a0(a8), .b1(b9), .a1(a9), .b2(b10), .a2(a10), .b3(b11), .a3(a11), .b4(b12), .a4(a12),
    .b5(b13), .a5(a13), .b6(b14), .a6(a14), .b7(b15), .a7(a15), .inv(vem), .s0(soma8inv_3_s0),
    .s1(soma8inv_3_s1), .s2(soma8inv_3_s2), .s3(soma8inv_3_s3), .s4(soma8inv_3_s4), .s5(soma8inv_3_s5),
    .s6(soma8inv_3_s6), .s7(soma8inv_3_s7), .Ovfl(soma8inv_3_ovfl));  // open: vai

  // Notes on the sheet:
  //   _1: default 1
endmodule
