// Digital circuit projVetControle.dig as structural Verilog
module projVetControle (
  input  CLK,
  input  START,
  output DONE,
  output [15:0] P
);

  wire ac, clr, en;
  wire [1:0] register_1_q, rom_1_d;

  LED led_1 (.in(DONE));
  projVetDataPath projvetdatapath_1 (.CLK(CLK), .CLR(clr), .EN(en), .P(P), .acabou(ac));
  Register #(.Bits(2)) register_1 (.D(rom_1_d), .C(CLK), .en(1'b1), .Q(register_1_q));
  ROM #(.AddrBits(4), .Bits(4)) rom_1 (.A({register_1_q, START, ac}), .sel(1'b1), .D({rom_1_d, en, clr}));
  and and_1 (DONE, rom_1_d[0], rom_1_d[1]);

  // Other names for the same wires on the sheet: c = CLK; d = DONE; st = START

  // Notes on the sheet:
  //   contents of rom_1 (hex, n*v repeats v):
  //   0,0,5,5,a,a,a,a,a,c,a,c,0,0,0,c
endmodule

/* Test case:
CLK START  DONE   P
C     0    0      0
C     1    0      0
C     1    0      0xFFFFFFFFFFFFFFE7
C     1    0      0xFFFFFFFFFFFFFFCE
C     1    0      0xFFFFFFFFFFFFFFB5
C     1    0      0xFFFFFFFFFFFFFF9C
C     1    0      0xFFFFFFFFFFFFFF83
C     1    0      0xFFFFFFFFFFFFFF6A
C     1    0      0xFFFFFFFFFFFFFF51
C     1    1      0xFFFFFFFFFFFFFF38
C     1    1      0xFFFFFFFFFFFFFF38
C     1    1      0xFFFFFFFFFFFFFF38
C     1    1      0xFFFFFFFFFFFFFF38
C     1    1      0xFFFFFFFFFFFFFF38
C     0    0      0xFFFFFFFFFFFFFF38
*/
