// Digital circuit projVetDataPath.dig as structural Verilog
module projVetDataPath (
  input  CLK,
  input  CLR,
  input  EN,
  output [15:0] P,
  output acabou
);

  wire comparator_2_eq, e;
  wire [3:0] ct1;
  wire [7:0] add_1_s, add_2_s, multiplexer_2_out, multiplexer_3_out, multiplexer_4_out, multiplexer_5_out,
       not_1_out, not_2_out, rom_1_d, rom_2_d;
  wire [15:0] add_3_s, add_4_s, mul_1_mul, multiplexer_6_out, multiplexer_7_out, not_3_out;

  Multiplexer multiplexer_1 (.sel(acabou), .in_0(EN), .in_1(1'b0), .out(e));
  Counter #(.Bits(4)) counter_1 (.en(e), .C(CLK), .clr(CLR), .out(ct1));  // open: ovf
  Comparator #(.Bits(4)) comparator_1 (.a(ct1), .b(4'b1000), .eq(acabou));  // open: gt, lt
  ROM #(.AddrBits(3), .Bits(8)) rom_1 (.A(ct1[2:0]), .sel(EN), .D(rom_1_d));
  ROM #(.AddrBits(3), .Bits(8)) rom_2 (.A(ct1[2:0]), .sel(EN), .D(rom_2_d));
  assign not_1_out = ~rom_1_d;  // Not not_1, 8 bits wide
  assign not_2_out = ~rom_2_d;  // Not not_2, 8 bits wide
  Add #(.Bits(8)) add_1 (.a(not_1_out), .b(8'h1), .c_i(1'b0), .s(add_1_s));  // open: c_o
  Add #(.Bits(8)) add_2 (.a(not_2_out), .b(8'h1), .c_i(1'b0), .s(add_2_s));  // open: c_o
  Comparator comparator_2 (.a(rom_2_d[7]), .b(rom_1_d[7]), .eq(comparator_2_eq));  // open: gt, lt
  Multiplexer #(.Bits(8)) multiplexer_2 (.sel(rom_1_d[7]), .in_0(rom_1_d), .in_1(add_1_s), .out(multiplexer_2_out));
  Multiplexer #(.Bits(8)) multiplexer_3 (.sel(rom_2_d[7]), .in_0(rom_2_d), .in_1(add_2_s), .out(multiplexer_3_out));
  Multiplexer #(.Bits(8)) multiplexer_4 (
    .sel(acabou), .in_0(multiplexer_2_out), .in_1({8{1'b0}}), .out(multiplexer_4_out));
  Multiplexer #(.Bits(8)) multiplexer_5 (
    .sel(acabou), .in_0(multiplexer_3_out), .in_1({8{1'b0}}), .out(multiplexer_5_out));
  Mul #(.Bits(8)) mul_1 (.a(multiplexer_4_out), .b(multiplexer_5_out), .mul(mul_1_mul));
  Add #(.Bits(16)) add_3 (.a(not_3_out), .b(16'h1), .c_i(1'b0), .s(add_3_s));  // open: c_o
  assign not_3_out = ~mul_1_mul;  // Not not_3, 16 bits wide
  Multiplexer #(.Bits(16)) multiplexer_6 (
    .sel(comparator_2_eq), .in_0(add_3_s), .in_1(mul_1_mul), .out(multiplexer_6_out));
  Add #(.Bits(16)) add_4 (.a(P), .b(multiplexer_6_out), .c_i(1'b0), .s(add_4_s));  // open: c_o
  Multiplexer #(.Bits(16)) multiplexer_7 (.sel(CLR), .in_0(add_4_s), .in_1({16{1'b0}}), .out(multiplexer_7_out));
  Register #(.Bits(16)) register_1 (.D(multiplexer_7_out), .C(CLK), .en(1'b1), .Q(P));

  // Other names for the same wires on the sheet: c = CLK; f[15:0] = P; ov = acabou

  // Notes on the sheet:
  //   contents of rom_1 (hex, n*v repeats v):
  //   ffffffffffffffe7,ffffffffffffffe7,ffffffffffffffe7,ffffffffffffffe7,ffffffffffffffe7,
  //   ffffffffffffffe7,ffffffffffffffe7,ffffffffffffffe7
  //   contents of rom_2 (hex, n*v repeats v):
  //   1,1,1,1,1,1,1,1
endmodule

/* Test case:
CLK   CLR  EN  P
C     1    0   0
C     0    1   0xFFFFFFFFFFFFFFE7
C     0    1   0xFFFFFFFFFFFFFFCE
C     0    1   0xFFFFFFFFFFFFFFB5
C     0    1   0xFFFFFFFFFFFFFF9C
C     0    1   0xFFFFFFFFFFFFFF83
C     0    1   0xFFFFFFFFFFFFFF6A
C     0    1   0xFFFFFFFFFFFFFF51
C     0    1   0xFFFFFFFFFFFFFF38
C     0    1   0xFFFFFFFFFFFFFF38
C     0    1   0xFFFFFFFFFFFFFF38
C     0    0   0xFFFFFFFFFFFFFF38
C     0    0   0xFFFFFFFFFFFFFF38
C     1    0   0
*/
